// Logisim project Proj2starter.circ as structural Verilog: 4 circuits, main circuit regfile
module CPUmain (
);

  wire alu_1_res, control_1_p6, control_1_p7;
  wire [3:0] control_1_p8;
  wire [4:0] control_1_p2, control_1_p3, control_1_p4;
  wire [31:0] control_1_p5, multiplexer_1_out, regfile_1_rs_data, regfile_1_rt_data, undriven;

  // Control control_1: pin names not known; wires that end beside it: {32{1'b0}}, control_1_p2, control_1_p3, control_1_p4, control_1_p5, control_1_p6, control_1_p7, control_1_p8
  regfile regfile_1 (
    .write_e(control_1_p6), .rd(control_1_p4), .rs(control_1_p2), .rt(control_1_p3), .rd_data(undriven),
    .rs_data(regfile_1_rs_data), .rt_data(regfile_1_rt_data));
  Multiplexer #(.width(32)) multiplexer_1 (
    .in0(regfile_1_rt_data), .in1(control_1_p5), .out(multiplexer_1_out), .sel(control_1_p7));
  ALU alu_1 (.OP1(regfile_1_rs_data), .OP2(multiplexer_1_out), .ALU_CODE(control_1_p8), .Res(alu_1_res));
endmodule

module regfile (
  input  [31:0] rd_data,
  input  write_e,
  input  [4:0] rd,
  input  [4:0] rs,
  input  [4:0] rt,
  output [31:0] rs_data,
  output [31:0] rt_data
);

  wire clock_1_out, demultiplexer_1_out1, demultiplexer_1_out2, demultiplexer_1_out3, demultiplexer_1_out4,
       demultiplexer_1_out5, demultiplexer_1_out6, demultiplexer_1_out7, demultiplexer_1_out8,
       demultiplexer_1_out9, demultiplexer_1_out10, demultiplexer_1_out11, demultiplexer_1_out12,
       demultiplexer_1_out13, demultiplexer_1_out14, demultiplexer_1_out15, demultiplexer_1_out16,
       demultiplexer_1_out17, demultiplexer_1_out18, demultiplexer_1_out19, demultiplexer_1_out20,
       demultiplexer_1_out21, demultiplexer_1_out22, demultiplexer_1_out23, demultiplexer_1_out24,
       demultiplexer_1_out25, demultiplexer_1_out26, demultiplexer_1_out27, demultiplexer_1_out28,
       demultiplexer_1_out29, demultiplexer_1_out30, demultiplexer_1_out31;
  wire [31:0] multiplexer_1_out, multiplexer_2_out, multiplexer_3_out, multiplexer_4_out, multiplexer_5_out,
       multiplexer_6_out, multiplexer_7_out, multiplexer_8_out, multiplexer_9_out, multiplexer_10_out,
       multiplexer_11_out, multiplexer_12_out, multiplexer_13_out, multiplexer_14_out, multiplexer_15_out,
       multiplexer_16_out, multiplexer_17_out, multiplexer_18_out, multiplexer_19_out, multiplexer_20_out,
       multiplexer_21_out, multiplexer_22_out, multiplexer_23_out, multiplexer_24_out, multiplexer_25_out,
       multiplexer_26_out, multiplexer_27_out, multiplexer_28_out, multiplexer_29_out, multiplexer_30_out,
       multiplexer_31_out, r1_q, r2_q, r3_q, r4_q, r5_q, r6_q, r7_q, r8_q, r9_q, r10_q, r11_q, r12_q, r13_q,
       r14_q, r15_q, r16_q, r17_q, r18_q, r19_q, r20_q, r21_q, r22_q, r23_q, r24_q, r25_q, r26_q, r27_q,
       r28_q, r29_q, r30_q, r31_q;

  Demultiplexer #(.select(5)) demultiplexer_1 (
    .out1(demultiplexer_1_out1), .out2(demultiplexer_1_out2), .out3(demultiplexer_1_out3),
    .out4(demultiplexer_1_out4), .out5(demultiplexer_1_out5), .out6(demultiplexer_1_out6),
    .out7(demultiplexer_1_out7), .out8(demultiplexer_1_out8), .out9(demultiplexer_1_out9),
    .out10(demultiplexer_1_out10), .out11(demultiplexer_1_out11), .out12(demultiplexer_1_out12),
    .out13(demultiplexer_1_out13), .out14(demultiplexer_1_out14), .out15(demultiplexer_1_out15),
    .out16(demultiplexer_1_out16), .out17(demultiplexer_1_out17), .out18(demultiplexer_1_out18),
    .out19(demultiplexer_1_out19), .out20(demultiplexer_1_out20), .out21(demultiplexer_1_out21),
    .out22(demultiplexer_1_out22), .out23(demultiplexer_1_out23), .out24(demultiplexer_1_out24),
    .out25(demultiplexer_1_out25), .out26(demultiplexer_1_out26), .out27(demultiplexer_1_out27),
    .out28(demultiplexer_1_out28), .out29(demultiplexer_1_out29), .out30(demultiplexer_1_out30),
    .out31(demultiplexer_1_out31), .in(write_e), .sel(rd));  // open: out0
  Multiplexer #(.width(32)) multiplexer_1 (
    .in0(r8_q), .in1(rd_data), .out(multiplexer_1_out), .sel(demultiplexer_1_out8));
  Register #(.width(32)) r8 (.D(multiplexer_1_out), .clk(clock_1_out), .Q(r8_q));  // open: en, clr
  Clock clock_1 (.out(clock_1_out));
  Multiplexer #(.width(32)) multiplexer_2 (
    .in0(r16_q), .in1(rd_data), .out(multiplexer_2_out), .sel(demultiplexer_1_out16));
  Register #(.width(32)) r16 (.D(multiplexer_2_out), .clk(clock_1_out), .Q(r16_q));  // open: en, clr
  Multiplexer #(.width(32)) multiplexer_3 (
    .in0(r24_q), .in1(rd_data), .out(multiplexer_3_out), .sel(demultiplexer_1_out24));
  Register #(.width(32)) r24 (.D(multiplexer_3_out), .clk(clock_1_out), .Q(r24_q));  // open: en, clr
  Multiplexer #(.width(32)) multiplexer_4 (
    .in0(r1_q), .in1(rd_data), .out(multiplexer_4_out), .sel(demultiplexer_1_out1));
  Register #(.width(32)) r1 (.D(multiplexer_4_out), .clk(clock_1_out), .Q(r1_q));  // open: en, clr
  Multiplexer #(.width(32)) multiplexer_5 (
    .in0(r9_q), .in1(rd_data), .out(multiplexer_5_out), .sel(demultiplexer_1_out9));
  Register #(.width(32)) r9 (.D(multiplexer_5_out), .clk(clock_1_out), .Q(r9_q));  // open: en, clr
  Multiplexer #(.width(32)) multiplexer_6 (
    .in0(r17_q), .in1(rd_data), .out(multiplexer_6_out), .sel(demultiplexer_1_out17));
  Register #(.width(32)) r17 (.D(multiplexer_6_out), .clk(clock_1_out), .Q(r17_q));  // open: en, clr
  Multiplexer #(.width(32)) multiplexer_7 (
    .in0(r25_q), .in1(rd_data), .out(multiplexer_7_out), .sel(demultiplexer_1_out25));
  Register #(.width(32)) r25 (.D(multiplexer_7_out), .clk(clock_1_out), .Q(r25_q));  // open: en, clr
  Multiplexer #(.width(32)) multiplexer_8 (
    .in0(r2_q), .in1(rd_data), .out(multiplexer_8_out), .sel(demultiplexer_1_out2));
  Register #(.width(32)) r2 (.D(multiplexer_8_out), .clk(clock_1_out), .Q(r2_q));  // open: en, clr
  Multiplexer #(.width(32)) multiplexer_9 (
    .in0(r10_q), .in1(rd_data), .out(multiplexer_9_out), .sel(demultiplexer_1_out10));
  Register #(.width(32)) r10 (.D(multiplexer_9_out), .clk(clock_1_out), .Q(r10_q));  // open: en, clr
  Multiplexer #(.width(32)) multiplexer_10 (
    .in0(r18_q), .in1(rd_data), .out(multiplexer_10_out), .sel(demultiplexer_1_out18));
  Register #(.width(32)) r18 (.D(multiplexer_10_out), .clk(clock_1_out), .Q(r18_q));  // open: en, clr
  Multiplexer #(.width(32)) multiplexer_11 (
    .in0(r26_q), .in1(rd_data), .out(multiplexer_11_out), .sel(demultiplexer_1_out26));
  Register #(.width(32)) r26 (.D(multiplexer_11_out), .clk(clock_1_out), .Q(r26_q));  // open: en, clr
  Multiplexer #(.width(32)) multiplexer_12 (
    .in0(r3_q), .in1(rd_data), .out(multiplexer_12_out), .sel(demultiplexer_1_out3));
  Register #(.width(32)) r3 (.D(multiplexer_12_out), .clk(clock_1_out), .Q(r3_q));  // open: en, clr
  Multiplexer #(.width(32)) multiplexer_13 (
    .in0(r11_q), .in1(rd_data), .out(multiplexer_13_out), .sel(demultiplexer_1_out11));
  Register #(.width(32)) r11 (.D(multiplexer_13_out), .clk(clock_1_out), .Q(r11_q));  // open: en, clr
  Multiplexer #(.width(32)) multiplexer_14 (
    .in0(r19_q), .in1(rd_data), .out(multiplexer_14_out), .sel(demultiplexer_1_out19));
  Register #(.width(32)) r19 (.D(multiplexer_14_out), .clk(clock_1_out), .Q(r19_q));  // open: en, clr
  Multiplexer #(.width(32)) multiplexer_15 (
    .in0(r27_q), .in1(rd_data), .out(multiplexer_15_out), .sel(demultiplexer_1_out27));
  Register #(.width(32)) r27 (.D(multiplexer_15_out), .clk(clock_1_out), .Q(r27_q));  // open: en, clr
  Multiplexer #(.width(32)) multiplexer_16 (
    .in0(r4_q), .in1(rd_data), .out(multiplexer_16_out), .sel(demultiplexer_1_out4));
  Register #(.width(32)) r4 (.D(multiplexer_16_out), .clk(clock_1_out), .Q(r4_q));  // open: en, clr
  Multiplexer #(.width(32)) multiplexer_17 (
    .in0(r12_q), .in1(rd_data), .out(multiplexer_17_out), .sel(demultiplexer_1_out12));
  Register #(.width(32)) r12 (.D(multiplexer_17_out), .clk(clock_1_out), .Q(r12_q));  // open: en, clr
  Multiplexer #(.width(32)) multiplexer_18 (
    .in0(r20_q), .in1(rd_data), .out(multiplexer_18_out), .sel(demultiplexer_1_out20));
  Register #(.width(32)) r20 (.D(multiplexer_18_out), .clk(clock_1_out), .Q(r20_q));  // open: en, clr
  Multiplexer #(.width(32)) multiplexer_19 (
    .in0(r28_q), .in1(rd_data), .out(multiplexer_19_out), .sel(demultiplexer_1_out28));
  Register #(.width(32)) r28 (.D(multiplexer_19_out), .clk(clock_1_out), .Q(r28_q));  // open: en, clr
  Multiplexer #(.width(32)) multiplexer_20 (
    .in0(r5_q), .in1(rd_data), .out(multiplexer_20_out), .sel(demultiplexer_1_out5));
  Register #(.width(32)) r5 (.D(multiplexer_20_out), .clk(clock_1_out), .Q(r5_q));  // open: en, clr
  Multiplexer #(.width(32)) multiplexer_21 (
    .in0(r13_q), .in1(rd_data), .out(multiplexer_21_out), .sel(demultiplexer_1_out13));
  Register #(.width(32)) r13 (.D(multiplexer_21_out), .clk(clock_1_out), .Q(r13_q));  // open: en, clr
  Multiplexer #(.width(32)) multiplexer_22 (
    .in0(r21_q), .in1(rd_data), .out(multiplexer_22_out), .sel(demultiplexer_1_out21));
  Register #(.width(32)) r21 (.D(multiplexer_22_out), .clk(clock_1_out), .Q(r21_q));  // open: en, clr
  Multiplexer #(.width(32)) multiplexer_23 (
    .in0(r29_q), .in1(rd_data), .out(multiplexer_23_out), .sel(demultiplexer_1_out29));
  Register #(.width(32)) r29 (.D(multiplexer_23_out), .clk(clock_1_out), .Q(r29_q));  // open: en, clr
  Multiplexer #(.width(32)) multiplexer_24 (
    .in0(r6_q), .in1(rd_data), .out(multiplexer_24_out), .sel(demultiplexer_1_out6));
  Register #(.width(32)) r6 (.D(multiplexer_24_out), .clk(clock_1_out), .Q(r6_q));  // open: en, clr
  Multiplexer #(.width(32)) multiplexer_25 (
    .in0(r14_q), .in1(rd_data), .out(multiplexer_25_out), .sel(demultiplexer_1_out14));
  Register #(.width(32)) r14 (.D(multiplexer_25_out), .clk(clock_1_out), .Q(r14_q));  // open: en, clr
  Multiplexer #(.width(32)) multiplexer_26 (
    .in0(r22_q), .in1(rd_data), .out(multiplexer_26_out), .sel(demultiplexer_1_out22));
  Register #(.width(32)) r22 (.D(multiplexer_26_out), .clk(clock_1_out), .Q(r22_q));  // open: en, clr
  Multiplexer #(.width(32)) multiplexer_27 (
    .in0(r30_q), .in1(rd_data), .out(multiplexer_27_out), .sel(demultiplexer_1_out30));
  Register #(.width(32)) r30 (.D(multiplexer_27_out), .clk(clock_1_out), .Q(r30_q));  // open: en, clr
  Multiplexer #(.width(32)) multiplexer_28 (
    .in0(r7_q), .in1(rd_data), .out(multiplexer_28_out), .sel(demultiplexer_1_out7));
  Register #(.width(32)) r7 (.D(multiplexer_28_out), .clk(clock_1_out), .Q(r7_q));  // open: en, clr
  Multiplexer #(.width(32)) multiplexer_29 (
    .in0(r15_q), .in1(rd_data), .out(multiplexer_29_out), .sel(demultiplexer_1_out15));
  Register #(.width(32)) r15 (.D(multiplexer_29_out), .clk(clock_1_out), .Q(r15_q));  // open: en, clr
  Multiplexer #(.width(32)) multiplexer_30 (
    .in0(r23_q), .in1(rd_data), .out(multiplexer_30_out), .sel(demultiplexer_1_out23));
  Register #(.width(32)) r23 (.D(multiplexer_30_out), .clk(clock_1_out), .Q(r23_q));  // open: en, clr
  Multiplexer #(.width(32)) multiplexer_31 (
    .in0(r31_q), .in1(rd_data), .out(multiplexer_31_out), .sel(demultiplexer_1_out31));
  Register #(.width(32)) r31 (.D(multiplexer_31_out), .clk(clock_1_out), .Q(r31_q));  // open: en, clr
  Multiplexer #(.select(5), .width(32)) multiplexer_32 (
    .in0({32{1'b0}}), .in1(r1_q), .in2(r2_q), .in3(r3_q), .in4(r4_q), .in5(r5_q), .in6(r6_q), .in7(r7_q),
    .in8(r8_q), .in9(r9_q), .in10(r10_q), .in11(r11_q), .in12(r12_q), .in13(r13_q), .in14(r14_q),
    .in15(r15_q), .in16(r16_q), .in17(r17_q), .in18(r18_q), .in19(r19_q), .in20(r20_q), .in21(r21_q),
    .in22(r22_q), .in23(r23_q), .in24(r24_q), .in25(r25_q), .in26(r26_q), .in27(r27_q), .in28(r28_q),
    .in29(r29_q), .in30(r30_q), .in31(r31_q), .out(rs_data), .sel(rs));
  Multiplexer #(.select(5), .width(32)) multiplexer_33 (
    .in0({32{1'b0}}), .in1(r1_q), .in2(r2_q), .in3(r3_q), .in4(r4_q), .in5(r5_q), .in6(r6_q), .in7(r7_q),
    .in8(r8_q), .in9(r9_q), .in10(r10_q), .in11(r11_q), .in12(r12_q), .in13(r13_q), .in14(r14_q),
    .in15(r15_q), .in16(r16_q), .in17(r17_q), .in18(r18_q), .in19(r19_q), .in20(r20_q), .in21(r21_q),
    .in22(r22_q), .in23(r23_q), .in24(r24_q), .in25(r25_q), .in26(r26_q), .in27(r27_q), .in28(r28_q),
    .in29(r29_q), .in30(r30_q), .in31(r31_q), .out(rt_data), .sel(rt));
endmodule

module ALU (
  input  [3:0] ALU_CODE,
  input  [31:0] OP1,
  input  [31:0] OP2,
  output Res
);

  Adder adder_1 ();  // open: a, b, out, cin, cout
  Subtractor subtractor_1 ();  // open: a, b, out, bin, bout
  Multiplier multiplier_1 ();  // open: a, b, out, cin, cout
  Divider divider_1 ();  // open: a, b, out, upper, rem
  Register HI ();  // open: D, en, clk, Q, clr
  Register LO ();  // open: D, en, clk, Q, clr
endmodule

module Control (
  input  in_1,
  input  in_2,
  input  [31:0] Inst,
  output [4:0] rs,
  output [4:0] rt,
  output [4:0] rd,
  output [5:0] out_7,
  output [31:0] imm,
  output reg_write_e,
  output imm_sel,
  output [3:0] ALU_code
);

  wire comparator_1_eq, comparator_2_eq, comparator_3_eq, comparator_4_eq, comparator_5_eq, comparator_6_eq,
       comparator_7_eq, comparator_8_eq, or_1_out, or_3_out, or_4_out;
  wire [3:0] multiplexer_2_out, multiplexer_3_out, multiplexer_4_out, multiplexer_5_out, multiplexer_6_out,
       multiplexer_7_out, multiplexer_8_out, multiplexer_9_out;
  wire [31:0] bit_extender_1_out;

  Comparator #(.width(6)) comparator_1 (.a(Inst[5:0]), .b(6'b100010), .eq(comparator_1_eq));  // open: gt, lt
  Comparator #(.width(6)) comparator_2 (.a(Inst[5:0]), .b(6'b011000), .eq(comparator_2_eq));  // open: gt, lt
  Comparator #(.width(6)) comparator_3 (.a(Inst[5:0]), .b(6'b011010), .eq(comparator_3_eq));  // open: gt, lt
  Comparator #(.width(6)) comparator_4 (.a(Inst[5:0]), .b(6'b010010), .eq(comparator_4_eq));  // open: gt, lt
  Comparator #(.width(6)) comparator_5 (.a(Inst[5:0]), .b(6'b001000), .eq(comparator_5_eq));  // open: gt, lt
  Comparator #(.width(6)) comparator_6 (.a(Inst[5:0]), .b({6{1'b0}}), .eq(comparator_6_eq));  // open: gt, lt
  Comparator #(.width(6)) comparator_7 (.a(Inst[5:0]), .b(6'b000010), .eq(comparator_7_eq));  // open: gt, lt
  Comparator #(.width(6)) comparator_8 (.a(Inst[5:0]), .b(6'b101010), .eq(comparator_8_eq));  // open: gt, lt
  Multiplexer #(.width(5)) multiplexer_1 ();  // open: in0, in1, out, sel
  Multiplexer #(.width(4)) multiplexer_2 (.in0(4'b0000), .in1(4'b0001), .out(multiplexer_2_out), .sel(comparator_1_eq));
  Multiplexer #(.width(4)) multiplexer_3 (.in0(4'b0000), .in1(4'b0010), .out(multiplexer_3_out), .sel(comparator_2_eq));
  Multiplexer #(.width(4)) multiplexer_4 (.in0(4'b0000), .in1(4'b0011), .out(multiplexer_4_out), .sel(comparator_3_eq));
  Multiplexer #(.width(4)) multiplexer_5 (.in0(4'b0000), .in1(4'b0100), .out(multiplexer_5_out), .sel(comparator_4_eq));
  Multiplexer #(.width(4)) multiplexer_6 (.in0(4'b0000), .in1(4'b0101), .out(multiplexer_6_out), .sel(comparator_5_eq));
  Multiplexer #(.width(4)) multiplexer_7 (.in0(4'b0000), .in1(4'b0110), .out(multiplexer_7_out), .sel(comparator_6_eq));
  Multiplexer #(.width(4)) multiplexer_8 (.in0(4'b0000), .in1(4'b0111), .out(multiplexer_8_out), .sel(comparator_7_eq));
  Multiplexer #(.width(4)) multiplexer_9 (.in0(4'b0000), .in1(4'b1000), .out(multiplexer_9_out), .sel(comparator_8_eq));
  Comparator #(.width(5)) comparator_9 ();  // open: a, b, gt, eq, lt
  Comparator #(.width(6)) comparator_10 (.a(Inst[31:26]), .b({6{1'b0}}));  // open: gt, eq, lt
  or or_1 (or_1_out, comparator_2_eq, comparator_3_eq);
  not not_1 (reg_write_e, or_1_out);
  Demultiplexer #(.width(5)) demultiplexer_1 ();  // open: out0, out1, in, sel
  assign ALU_code = multiplexer_2_out | multiplexer_3_out | multiplexer_4_out | multiplexer_5_out | multiplexer_6_out | multiplexer_7_out | multiplexer_8_out | multiplexer_9_out;  // OR_Gate or_2, 4 bits wide
  or or_3 (or_3_out, in_1, in_2);
  or or_4 (or_4_out, in_1, in_2);
  Multiplexer #(.width(5)) multiplexer_10 (.in0(Inst[15:11]), .in1(Inst[20:16]), .out(rd), .sel(in_1));
  Multiplexer #(.width(5)) multiplexer_11 (.in0({5{1'b0}}), .in1(Inst[25:21]), .out(rs), .sel(or_3_out));
  Multiplexer #(.width(5)) multiplexer_12 (.in0({5{1'b0}}), .in1(Inst[20:16]), .out(rt), .sel(or_4_out));
  assign bit_extender_1_out = {{16{Inst[5]}}, {Inst[5:0], Inst[10:6], Inst[15:11]}};  // Bit_Extender bit_extender_1
  Multiplexer #(.width(32)) multiplexer_13 (.in0({32{1'b0}}), .in1(bit_extender_1_out), .out(imm), .sel(in_1));

  assign imm_sel = in_1;
  assign out_7 = Inst[5:0];

  // Notes on the sheet:
  //   OP code
  //   rs
  //   shamt
  //   func
  //   sub
  //   mult
  //   div
  //   mflo
  //   mfhi
  //   sll
  //   srl
  //   slt
  //   rt
  //   rd
  //   I-type
  //   R-type
endmodule
