// Logisim project Project3memory.circ as structural Verilog: 4 circuits, main circuit regfile
module CPUmain (
);

  wire and_1_out, and_2_out, and_3_out, clock_1_out, clock_2_out, clock_3_out, comparator_1_eq,
       control_1_bne_sel, control_1_branch, control_1_imm_sel, control_1_j_reg_select, control_1_j_type,
       control_1_jal_select, control_1_mem_we, control_1_read_ram, control_1_reg_write_e, not_1_out,
       not_2_out, or_1_out, undriven_2;
  wire [3:0] control_1_alu_code;
  wire [4:0] control_1_rd, control_1_rs, control_1_rt;
  wire [7:0] adder_3_out, multiplexer_4_out, register_2_q, undriven;
  wire [15:0] bit_extender_3_out, bit_extender_5_out, rom_1_data, rom_1_data_2;
  wire [25:0] bit_extender_4_out, shifter_2_out;
  wire [31:0] adder_1_out, adder_2_out, alu_1_res, bit_extender_1_out, bit_extender_2_out, control_1_imm,
       multiplexer_1_out, multiplexer_2_out, multiplexer_3_out, multiplexer_5_out, multiplexer_6_out,
       multiplexer_7_out, ram_1_dout, regfile_1_rs_data, regfile_1_rt_data, register_1_q, shifter_1_out,
       shifter_3_out, shifter_4_out;

  Adder #(.width(32)) adder_1 (.a(register_1_q), .b(32'h4), .out(adder_1_out));  // open: cin, cout
  assign bit_extender_1_out = {{16{rom_1_data[15]}}, rom_1_data};  // Bit_Extender bit_extender_1
  // Probe on adder_1_out
  Shifter #(.width(32)) shifter_1 (.in(bit_extender_1_out), .\dist (5'b00010), .out(shifter_1_out));
  // Probe on shifter_1_out
  Shifter #(.width(26)) shifter_2 (.in(bit_extender_4_out), .\dist (5'b00010), .out(shifter_2_out));
  Adder #(.width(32)) adder_2 (.a(adder_1_out), .b(shifter_1_out), .out(adder_2_out));  // open: cin, cout
  assign bit_extender_2_out = {{6{shifter_2_out[25]}}, shifter_2_out};  // Bit_Extender bit_extender_2
  Multiplexer #(.width(32)) multiplexer_1 (
    .in0(adder_1_out), .in1(adder_2_out), .out(multiplexer_1_out), .sel(and_1_out));
  Multiplexer #(.width(32)) multiplexer_2 (
    .in0(bit_extender_2_out), .in1(regfile_1_rs_data), .out(multiplexer_2_out), .sel(control_1_j_reg_select));
  Shifter #(.shift("lr"), .width(32)) shifter_3 (.in(register_1_q), .\dist (5'b00010), .out(shifter_3_out));
  Register #(.width(32)) register_1 (
    .D(multiplexer_3_out), .en(1'b1), .clk(clock_1_out), .Q(register_1_q));  // open: clr
  Multiplexer #(.width(32)) multiplexer_3 (
    .in0(multiplexer_1_out), .in1(multiplexer_2_out), .out(multiplexer_3_out), .sel(control_1_j_type));
  Clock clock_1 (.out(clock_1_out));
  Bit_Extender #(.in_width(32)) bit_extender_3 (.in(shifter_3_out), .out(bit_extender_3_out));
  ROM #(.addrWidth(16), .dataWidth(32)) rom_1 (.addr(bit_extender_3_out), .data({rom_1_data_2, rom_1_data}));
  Adder adder_3 (.a(register_2_q), .b(8'h4), .out(adder_3_out));  // open: cin, cout
  Multiplexer #(.width(8)) multiplexer_4 (.in0(adder_3_out), .in1(undriven), .out(multiplexer_4_out), .sel(undriven_2));
  // Probe on {rom_1_data_2, rom_1_data}
  Bit_Extender #(.in_width(32), .out_width(26)) bit_extender_4 (
    .in({rom_1_data_2, rom_1_data}), .out(bit_extender_4_out));
  Register register_2 (.D(multiplexer_4_out), .clk(clock_2_out), .Q(register_2_q));  // open: en, clr
  Clock clock_2 (.out(clock_2_out));
  and and_1 (and_1_out, control_1_branch, or_1_out);
  or or_1 (or_1_out, and_2_out, and_3_out);
  and and_2 (and_2_out, comparator_1_eq, not_1_out);
  and and_3 (and_3_out, not_2_out, control_1_bne_sel);
  not not_1 (not_1_out, control_1_bne_sel);
  not not_2 (not_2_out, comparator_1_eq);
  Multiplexer #(.width(32)) multiplexer_5 (
    .in0(alu_1_res), .in1(ram_1_dout), .out(multiplexer_5_out), .sel(control_1_read_ram));
  // Probe on {rom_1_data_2, rom_1_data}
  Multiplexer #(.width(32)) multiplexer_6 (
    .in0(multiplexer_5_out), .in1(adder_1_out), .out(multiplexer_6_out), .sel(control_1_jal_select));
  Control control_1 (
    .Inst({rom_1_data_2, rom_1_data}), .rs(control_1_rs), .rt(control_1_rt), .rd(control_1_rd),
    .imm(control_1_imm), .reg_write_e(control_1_reg_write_e), .imm_sel(control_1_imm_sel),
    .mem_we(control_1_mem_we), .read_ram(control_1_read_ram), .Branch(control_1_branch),
    .BNE_sel(control_1_bne_sel), .j_reg_select(control_1_j_reg_select), .jal_select(control_1_jal_select),
    .J_type(control_1_j_type), .ALU_code(control_1_alu_code));
  regfile regfile_1 (
    .write_e(control_1_reg_write_e), .rd(control_1_rd), .rs(control_1_rs), .rt(control_1_rt),
    .rd_data(multiplexer_6_out), .rs_data(regfile_1_rs_data), .rt_data(regfile_1_rt_data));
  Comparator #(.width(32)) comparator_1 (
    .a(regfile_1_rs_data), .b(regfile_1_rt_data), .eq(comparator_1_eq));  // open: gt, lt
  Multiplexer #(.width(32)) multiplexer_7 (
    .in0(regfile_1_rt_data), .in1(control_1_imm), .out(multiplexer_7_out), .sel(control_1_imm_sel));
  // Probe on alu_1_res
  ALU alu_1 (.OP1(regfile_1_rs_data), .OP2(multiplexer_7_out), .ALU_CODE(control_1_alu_code), .Res(alu_1_res));
  // Probe on bit_extender_5_out
  RAM #(.addrWidth(16), .dataWidth(32), .enables("line")) ram_1 (
    .addr(bit_extender_5_out), .we(control_1_mem_we), .clk(clock_3_out), .din(regfile_1_rt_data),
    .dout(ram_1_dout));
  Bit_Extender #(.in_width(32)) bit_extender_5 (.in(shifter_4_out), .out(bit_extender_5_out));
  Shifter #(.shift("lr"), .width(32)) shifter_4 (.in(alu_1_res), .\dist (5'b00010), .out(shifter_4_out));
  Clock clock_3 (.out(clock_3_out));

  // Notes on the sheet:
  //   PC adder + 4
  //   label or j/jal (word addressed)
  //   Branch
  //   offset
  //   rs for jr/jalr (byte addressed)
  //   jr/jalr
  //   any j
  //   j
  //   contents of rom_1 (hex, n*v repeats v):
  //   8d110004 8d120008 200a0004 8d530008
  //   j_reg
  //   beq
  //   bne
  //   jal/jalr
  //   beq/bne
endmodule

module regfile (
  input  [31:0] rd_data,
  input  write_e,
  input  [4:0] rd,
  input  [4:0] rs,
  input  [4:0] rt,
  output [31:0] rs_data,
  output [31:0] rt_data
);

  wire clock_1_out, demultiplexer_1_out1, demultiplexer_1_out2, demultiplexer_1_out3, demultiplexer_1_out4,
       demultiplexer_1_out5, demultiplexer_1_out6, demultiplexer_1_out7, demultiplexer_1_out8,
       demultiplexer_1_out9, demultiplexer_1_out10, demultiplexer_1_out11, demultiplexer_1_out12,
       demultiplexer_1_out13, demultiplexer_1_out14, demultiplexer_1_out15, demultiplexer_1_out16,
       demultiplexer_1_out17, demultiplexer_1_out18, demultiplexer_1_out19, demultiplexer_1_out20,
       demultiplexer_1_out21, demultiplexer_1_out22, demultiplexer_1_out23, demultiplexer_1_out24,
       demultiplexer_1_out25, demultiplexer_1_out26, demultiplexer_1_out27, demultiplexer_1_out28,
       demultiplexer_1_out29, demultiplexer_1_out30, demultiplexer_1_out31;
  wire [31:0] multiplexer_1_out, multiplexer_2_out, multiplexer_3_out, multiplexer_4_out, multiplexer_5_out,
       multiplexer_6_out, multiplexer_7_out, multiplexer_8_out, multiplexer_9_out, multiplexer_10_out,
       multiplexer_11_out, multiplexer_12_out, multiplexer_13_out, multiplexer_14_out, multiplexer_15_out,
       multiplexer_16_out, multiplexer_17_out, multiplexer_18_out, multiplexer_19_out, multiplexer_20_out,
       multiplexer_21_out, multiplexer_22_out, multiplexer_23_out, multiplexer_24_out, multiplexer_25_out,
       multiplexer_26_out, multiplexer_27_out, multiplexer_28_out, multiplexer_29_out, multiplexer_30_out,
       multiplexer_31_out, r1_q, r2_q, r3_q, r4_q, r5_q, r6_q, r7_q, r8_q, r9_q, r10_q, r11_q, r12_q, r13_q,
       r14_q, r15_q, r16_q, r17_q, r18_q, r19_q, r20_q, r21_q, r22_q, r23_q, r24_q, r25_q, r26_q, r27_q,
       r28_q, r29_q, r30_q, r31_q;

  Demultiplexer #(.select(5)) demultiplexer_1 (
    .out1(demultiplexer_1_out1), .out2(demultiplexer_1_out2), .out3(demultiplexer_1_out3),
    .out4(demultiplexer_1_out4), .out5(demultiplexer_1_out5), .out6(demultiplexer_1_out6),
    .out7(demultiplexer_1_out7), .out8(demultiplexer_1_out8), .out9(demultiplexer_1_out9),
    .out10(demultiplexer_1_out10), .out11(demultiplexer_1_out11), .out12(demultiplexer_1_out12),
    .out13(demultiplexer_1_out13), .out14(demultiplexer_1_out14), .out15(demultiplexer_1_out15),
    .out16(demultiplexer_1_out16), .out17(demultiplexer_1_out17), .out18(demultiplexer_1_out18),
    .out19(demultiplexer_1_out19), .out20(demultiplexer_1_out20), .out21(demultiplexer_1_out21),
    .out22(demultiplexer_1_out22), .out23(demultiplexer_1_out23), .out24(demultiplexer_1_out24),
    .out25(demultiplexer_1_out25), .out26(demultiplexer_1_out26), .out27(demultiplexer_1_out27),
    .out28(demultiplexer_1_out28), .out29(demultiplexer_1_out29), .out30(demultiplexer_1_out30),
    .out31(demultiplexer_1_out31), .in(write_e), .sel(rd));  // open: out0
  Multiplexer #(.width(32)) multiplexer_1 (
    .in0(r8_q), .in1(rd_data), .out(multiplexer_1_out), .sel(demultiplexer_1_out8));
  Register #(.width(32)) r8 (.D(multiplexer_1_out), .clk(clock_1_out), .Q(r8_q));  // open: en, clr
  Clock clock_1 (.out(clock_1_out));
  Multiplexer #(.width(32)) multiplexer_2 (
    .in0(r16_q), .in1(rd_data), .out(multiplexer_2_out), .sel(demultiplexer_1_out16));
  Register #(.width(32)) r16 (.D(multiplexer_2_out), .clk(clock_1_out), .Q(r16_q));  // open: en, clr
  Multiplexer #(.width(32)) multiplexer_3 (
    .in0(r24_q), .in1(rd_data), .out(multiplexer_3_out), .sel(demultiplexer_1_out24));
  Register #(.width(32)) r24 (.D(multiplexer_3_out), .clk(clock_1_out), .Q(r24_q));  // open: en, clr
  Multiplexer #(.width(32)) multiplexer_4 (
    .in0(r1_q), .in1(rd_data), .out(multiplexer_4_out), .sel(demultiplexer_1_out1));
  Register #(.width(32)) r1 (.D(multiplexer_4_out), .clk(clock_1_out), .Q(r1_q));  // open: en, clr
  Multiplexer #(.width(32)) multiplexer_5 (
    .in0(r9_q), .in1(rd_data), .out(multiplexer_5_out), .sel(demultiplexer_1_out9));
  Register #(.width(32)) r9 (.D(multiplexer_5_out), .clk(clock_1_out), .Q(r9_q));  // open: en, clr
  Multiplexer #(.width(32)) multiplexer_6 (
    .in0(r17_q), .in1(rd_data), .out(multiplexer_6_out), .sel(demultiplexer_1_out17));
  Register #(.width(32)) r17 (.D(multiplexer_6_out), .clk(clock_1_out), .Q(r17_q));  // open: en, clr
  Multiplexer #(.width(32)) multiplexer_7 (
    .in0(r25_q), .in1(rd_data), .out(multiplexer_7_out), .sel(demultiplexer_1_out25));
  Register #(.width(32)) r25 (.D(multiplexer_7_out), .clk(clock_1_out), .Q(r25_q));  // open: en, clr
  Multiplexer #(.width(32)) multiplexer_8 (
    .in0(r2_q), .in1(rd_data), .out(multiplexer_8_out), .sel(demultiplexer_1_out2));
  Register #(.width(32)) r2 (.D(multiplexer_8_out), .clk(clock_1_out), .Q(r2_q));  // open: en, clr
  Multiplexer #(.width(32)) multiplexer_9 (
    .in0(r10_q), .in1(rd_data), .out(multiplexer_9_out), .sel(demultiplexer_1_out10));
  Register #(.width(32)) r10 (.D(multiplexer_9_out), .clk(clock_1_out), .Q(r10_q));  // open: en, clr
  Multiplexer #(.width(32)) multiplexer_10 (
    .in0(r18_q), .in1(rd_data), .out(multiplexer_10_out), .sel(demultiplexer_1_out18));
  Register #(.width(32)) r18 (.D(multiplexer_10_out), .clk(clock_1_out), .Q(r18_q));  // open: en, clr
  Multiplexer #(.width(32)) multiplexer_11 (
    .in0(r26_q), .in1(rd_data), .out(multiplexer_11_out), .sel(demultiplexer_1_out26));
  Register #(.width(32)) r26 (.D(multiplexer_11_out), .clk(clock_1_out), .Q(r26_q));  // open: en, clr
  Multiplexer #(.width(32)) multiplexer_12 (
    .in0(r3_q), .in1(rd_data), .out(multiplexer_12_out), .sel(demultiplexer_1_out3));
  Register #(.width(32)) r3 (.D(multiplexer_12_out), .clk(clock_1_out), .Q(r3_q));  // open: en, clr
  Multiplexer #(.width(32)) multiplexer_13 (
    .in0(r11_q), .in1(rd_data), .out(multiplexer_13_out), .sel(demultiplexer_1_out11));
  Register #(.width(32)) r11 (.D(multiplexer_13_out), .clk(clock_1_out), .Q(r11_q));  // open: en, clr
  Multiplexer #(.width(32)) multiplexer_14 (
    .in0(r19_q), .in1(rd_data), .out(multiplexer_14_out), .sel(demultiplexer_1_out19));
  Register #(.width(32)) r19 (.D(multiplexer_14_out), .clk(clock_1_out), .Q(r19_q));  // open: en, clr
  Multiplexer #(.width(32)) multiplexer_15 (
    .in0(r27_q), .in1(rd_data), .out(multiplexer_15_out), .sel(demultiplexer_1_out27));
  Register #(.width(32)) r27 (.D(multiplexer_15_out), .clk(clock_1_out), .Q(r27_q));  // open: en, clr
  Multiplexer #(.width(32)) multiplexer_16 (
    .in0(r4_q), .in1(rd_data), .out(multiplexer_16_out), .sel(demultiplexer_1_out4));
  Register #(.width(32)) r4 (.D(multiplexer_16_out), .clk(clock_1_out), .Q(r4_q));  // open: en, clr
  Multiplexer #(.width(32)) multiplexer_17 (
    .in0(r12_q), .in1(rd_data), .out(multiplexer_17_out), .sel(demultiplexer_1_out12));
  Register #(.width(32)) r12 (.D(multiplexer_17_out), .clk(clock_1_out), .Q(r12_q));  // open: en, clr
  Multiplexer #(.width(32)) multiplexer_18 (
    .in0(r20_q), .in1(rd_data), .out(multiplexer_18_out), .sel(demultiplexer_1_out20));
  Register #(.width(32)) r20 (.D(multiplexer_18_out), .clk(clock_1_out), .Q(r20_q));  // open: en, clr
  Multiplexer #(.width(32)) multiplexer_19 (
    .in0(r28_q), .in1(rd_data), .out(multiplexer_19_out), .sel(demultiplexer_1_out28));
  Register #(.width(32)) r28 (.D(multiplexer_19_out), .clk(clock_1_out), .Q(r28_q));  // open: en, clr
  Multiplexer #(.width(32)) multiplexer_20 (
    .in0(r5_q), .in1(rd_data), .out(multiplexer_20_out), .sel(demultiplexer_1_out5));
  Register #(.width(32)) r5 (.D(multiplexer_20_out), .clk(clock_1_out), .Q(r5_q));  // open: en, clr
  Multiplexer #(.width(32)) multiplexer_21 (
    .in0(r13_q), .in1(rd_data), .out(multiplexer_21_out), .sel(demultiplexer_1_out13));
  Register #(.width(32)) r13 (.D(multiplexer_21_out), .clk(clock_1_out), .Q(r13_q));  // open: en, clr
  Multiplexer #(.width(32)) multiplexer_22 (
    .in0(r21_q), .in1(rd_data), .out(multiplexer_22_out), .sel(demultiplexer_1_out21));
  Register #(.width(32)) r21 (.D(multiplexer_22_out), .clk(clock_1_out), .Q(r21_q));  // open: en, clr
  Multiplexer #(.width(32)) multiplexer_23 (
    .in0(r29_q), .in1(rd_data), .out(multiplexer_23_out), .sel(demultiplexer_1_out29));
  Register #(.width(32)) r29 (.D(multiplexer_23_out), .clk(clock_1_out), .Q(r29_q));  // open: en, clr
  Multiplexer #(.width(32)) multiplexer_24 (
    .in0(r6_q), .in1(rd_data), .out(multiplexer_24_out), .sel(demultiplexer_1_out6));
  Register #(.width(32)) r6 (.D(multiplexer_24_out), .clk(clock_1_out), .Q(r6_q));  // open: en, clr
  Multiplexer #(.width(32)) multiplexer_25 (
    .in0(r14_q), .in1(rd_data), .out(multiplexer_25_out), .sel(demultiplexer_1_out14));
  Register #(.width(32)) r14 (.D(multiplexer_25_out), .clk(clock_1_out), .Q(r14_q));  // open: en, clr
  Multiplexer #(.width(32)) multiplexer_26 (
    .in0(r22_q), .in1(rd_data), .out(multiplexer_26_out), .sel(demultiplexer_1_out22));
  Register #(.width(32)) r22 (.D(multiplexer_26_out), .clk(clock_1_out), .Q(r22_q));  // open: en, clr
  Multiplexer #(.width(32)) multiplexer_27 (
    .in0(r30_q), .in1(rd_data), .out(multiplexer_27_out), .sel(demultiplexer_1_out30));
  Register #(.width(32)) r30 (.D(multiplexer_27_out), .clk(clock_1_out), .Q(r30_q));  // open: en, clr
  Multiplexer #(.width(32)) multiplexer_28 (
    .in0(r7_q), .in1(rd_data), .out(multiplexer_28_out), .sel(demultiplexer_1_out7));
  Register #(.width(32)) r7 (.D(multiplexer_28_out), .clk(clock_1_out), .Q(r7_q));  // open: en, clr
  Multiplexer #(.width(32)) multiplexer_29 (
    .in0(r15_q), .in1(rd_data), .out(multiplexer_29_out), .sel(demultiplexer_1_out15));
  Register #(.width(32)) r15 (.D(multiplexer_29_out), .clk(clock_1_out), .Q(r15_q));  // open: en, clr
  Multiplexer #(.width(32)) multiplexer_30 (
    .in0(r23_q), .in1(rd_data), .out(multiplexer_30_out), .sel(demultiplexer_1_out23));
  Register #(.width(32)) r23 (.D(multiplexer_30_out), .clk(clock_1_out), .Q(r23_q));  // open: en, clr
  Multiplexer #(.width(32)) multiplexer_31 (
    .in0(r31_q), .in1(rd_data), .out(multiplexer_31_out), .sel(demultiplexer_1_out31));
  Register #(.width(32)) r31 (.D(multiplexer_31_out), .clk(clock_1_out), .Q(r31_q));  // open: en, clr
  Multiplexer #(.select(5), .width(32)) multiplexer_32 (
    .in0({32{1'b0}}), .in1(r1_q), .in2(r2_q), .in3(r3_q), .in4(r4_q), .in5(r5_q), .in6(r6_q), .in7(r7_q),
    .in8(r8_q), .in9(r9_q), .in10(r10_q), .in11(r11_q), .in12(r12_q), .in13(r13_q), .in14(r14_q),
    .in15(r15_q), .in16(r16_q), .in17(r17_q), .in18(r18_q), .in19(r19_q), .in20(r20_q), .in21(r21_q),
    .in22(r22_q), .in23(r23_q), .in24(r24_q), .in25(r25_q), .in26(r26_q), .in27(r27_q), .in28(r28_q),
    .in29(r29_q), .in30(r30_q), .in31(r31_q), .out(rs_data), .sel(rs));
  Multiplexer #(.select(5), .width(32)) multiplexer_33 (
    .in0({32{1'b0}}), .in1(r1_q), .in2(r2_q), .in3(r3_q), .in4(r4_q), .in5(r5_q), .in6(r6_q), .in7(r7_q),
    .in8(r8_q), .in9(r9_q), .in10(r10_q), .in11(r11_q), .in12(r12_q), .in13(r13_q), .in14(r14_q),
    .in15(r15_q), .in16(r16_q), .in17(r17_q), .in18(r18_q), .in19(r19_q), .in20(r20_q), .in21(r21_q),
    .in22(r22_q), .in23(r23_q), .in24(r24_q), .in25(r25_q), .in26(r26_q), .in27(r27_q), .in28(r28_q),
    .in29(r29_q), .in30(r30_q), .in31(r31_q), .out(rt_data), .sel(rt));
endmodule

module ALU (
  input  [3:0] ALU_CODE,
  input  [31:0] OP1,
  input  [31:0] OP2,
  output [31:0] Res
);

  wire clock_1_out, comparator_1_lt, comparator_2_eq, comparator_3_eq, or_2_out;
  wire [4:0] bit_extender_1_out, bit_extender_2_out;
  wire [5:0] bitadder_1_out;
  wire [31:0] adder_1_out, and_1_out, and_2_out, bit_extender_3_out, bit_extender_4_out, divider_1_out,
       divider_1_rem, HI_q, LO_q, multiplexer_1_out, multiplexer_2_out, multiplier_1_cout, multiplier_1_out,
       nor_1_out, or_1_out, shifter_1_out, shifter_2_out, shifter_3_out, subtractor_1_out, subtractor_2_out,
       xor_1_out;

  Bit_Extender #(.in_width(32), .out_width(5)) bit_extender_1 (.in(OP2), .out(bit_extender_1_out));
  Bit_Extender #(.in_width(32), .out_width(5)) bit_extender_2 (.in(OP2), .out(bit_extender_2_out));
  Adder #(.width(32)) adder_1 (.a(OP1), .b(OP2), .out(adder_1_out));  // open: cin, cout
  Subtractor #(.width(32)) subtractor_1 (.a(OP1), .b(OP2), .out(subtractor_1_out));  // open: bin, bout
  Multiplier #(.width(32)) multiplier_1 (
    .a(OP1), .b(OP2), .out(multiplier_1_out), .cout(multiplier_1_cout));  // open: cin
  Divider #(.width(32)) divider_1 (.a(OP1), .b(OP2), .out(divider_1_out), .rem(divider_1_rem));  // open: upper
  Shifter #(.width(32)) shifter_1 (.in(OP1), .\dist (bit_extender_1_out), .out(shifter_1_out));
  Shifter #(.shift("lr"), .width(32)) shifter_2 (.in(OP1), .\dist (bit_extender_2_out), .out(shifter_2_out));
  Comparator #(.width(32)) comparator_1 (.a(OP1), .b(OP2), .lt(comparator_1_lt));  // open: gt, eq
  assign and_1_out = OP1 & OP2;  // AND_Gate and_1, 32 bits wide
  assign or_1_out = OP1 | OP2;  // OR_Gate or_1, 32 bits wide
  assign xor_1_out = OP1 ^ OP2;  // XOR_Gate xor_1, 32 bits wide
  assign nor_1_out = ~(OP1 | OP2);  // NOR_Gate nor_1, 32 bits wide
  BitAdder #(.width(32)) bitadder_1 (.in0(OP1), .out(bitadder_1_out));
  Subtractor #(.width(32)) subtractor_2 (
    .a(32'h20), .b(bit_extender_4_out), .out(subtractor_2_out));  // open: bin, bout
  Shifter #(.width(32)) shifter_3 (.\dist (5'b10000), .out(shifter_3_out));  // open: in
  Comparator #(.width(4)) comparator_2 (.a(ALU_CODE), .b(4'b0010), .eq(comparator_2_eq));  // open: gt, lt
  assign bit_extender_3_out = {{31{comparator_1_lt}}, comparator_1_lt};  // Bit_Extender bit_extender_3
  assign bit_extender_4_out = {{26{bitadder_1_out[5]}}, bitadder_1_out};  // Bit_Extender bit_extender_4
  // Probe on shifter_1_out
  // Probe on shifter_2_out
  assign and_2_out = 32'h1 & bit_extender_3_out;  // AND_Gate and_2, 32 bits wide
  Comparator #(.width(4)) comparator_3 (.a(ALU_CODE), .b(4'b0011), .eq(comparator_3_eq));  // open: gt, lt
  Register #(.width(32)) HI (.D(multiplexer_1_out), .en(or_2_out), .clk(clock_1_out), .Q(HI_q));  // open: clr
  Multiplexer #(.width(32)) multiplexer_1 (
    .in0(multiplier_1_cout), .in1(divider_1_rem), .out(multiplexer_1_out), .sel(comparator_3_eq));
  or or_2 (or_2_out, comparator_3_eq, comparator_2_eq);
  Register #(.width(32)) LO (.D(multiplexer_2_out), .en(or_2_out), .clk(clock_1_out), .Q(LO_q));  // open: clr
  Multiplexer #(.width(32)) multiplexer_2 (
    .in0(multiplier_1_out), .in1(divider_1_out), .out(multiplexer_2_out), .sel(comparator_3_eq));
  Clock clock_1 (.out(clock_1_out));
  Multiplexer #(.select(4), .width(32)) multiplexer_3 (
    .in0(adder_1_out), .in1(subtractor_1_out), .in2({32{1'b0}}), .in3({32{1'b0}}), .in4(LO_q), .in5(HI_q),
    .in6(shifter_1_out), .in7(shifter_2_out), .in8(and_2_out), .in9(and_1_out), .in10(or_1_out),
    .in11(xor_1_out), .in12(nor_1_out), .in13(bit_extender_4_out), .in14(subtractor_2_out),
    .in15(shifter_3_out), .out(Res), .sel(ALU_CODE));

  // Notes on the sheet:
  //   add addi
  //   sub
  //   mult
  //   div
  //   sll
  //   srl
  //   slt
  //   and andi
  //   or ori
  //   xor xori
  //   nor
  //   mult ALU code = 2
  //   div ALU code = 3
endmodule

module Control (
  input  [31:0] Inst,
  output [4:0] rs,
  output [4:0] rt,
  output [4:0] rd,
  output [31:0] imm,
  output reg_write_e,
  output imm_sel,
  output mem_we,
  output read_ram,
  output Branch,
  output BNE_sel,
  output j_reg_select,
  output jal_select,
  output J_type,
  output [3:0] ALU_code
);

  wire and_1_out, and_3_out, and_4_out, and_5_out, and_6_out, comparator_1_eq, comparator_2_eq,
       comparator_3_eq, comparator_4_eq, comparator_5_eq, comparator_6_eq, comparator_7_eq, comparator_8_eq,
       comparator_9_eq, comparator_10_eq, comparator_11_eq, comparator_12_eq, comparator_13_eq,
       comparator_13_gt, comparator_13_lt, comparator_14_eq, comparator_15_eq, comparator_16_eq,
       comparator_17_eq, comparator_18_eq, comparator_19_eq, comparator_20_eq, comparator_22_eq,
       comparator_23_eq, comparator_25_eq, comparator_26_eq, comparator_27_eq, not_1_out, not_2_out,
       not_3_out, not_4_out, or_1_out, or_2_out, or_4_out, or_5_out, or_9_out, or_12_out;
  wire [3:0] multiplexer_1_out, multiplexer_2_out, multiplexer_3_out, multiplexer_4_out, multiplexer_5_out,
       multiplexer_6_out, multiplexer_7_out, multiplexer_8_out, multiplexer_9_out, multiplexer_10_out,
       multiplexer_11_out, multiplexer_12_out, multiplexer_13_out, multiplexer_14_out, multiplexer_15_out,
       multiplexer_22_out, or_3_out, or_6_out;
  wire [4:0] multiplexer_16_out, multiplexer_17_out, multiplexer_18_out, multiplexer_19_out,
       multiplexer_20_out;
  wire [31:0] bit_extender_1_out, bit_extender_2_out, multiplexer_21_out;

  // Probe on Inst[31:26]
  // Probe on Inst[5:0]
  Comparator #(.width(6)) comparator_1 (.a(Inst[5:0]), .b(6'b100010), .eq(comparator_1_eq));  // open: gt, lt
  Comparator #(.width(6)) comparator_2 (.a(Inst[5:0]), .b(6'b011000), .eq(comparator_2_eq));  // open: gt, lt
  Comparator #(.width(6)) comparator_3 (.a(Inst[5:0]), .b(6'b011010), .eq(comparator_3_eq));  // open: gt, lt
  Comparator #(.width(6)) comparator_4 (.a(Inst[5:0]), .b(6'b010010), .eq(comparator_4_eq));  // open: gt, lt
  Comparator #(.width(6)) comparator_5 (.a(Inst[5:0]), .b(6'b010000), .eq(comparator_5_eq));  // open: gt, lt
  Comparator #(.width(6)) comparator_6 (.a(Inst[5:0]), .b({6{1'b0}}), .eq(comparator_6_eq));  // open: gt, lt
  Comparator #(.width(6)) comparator_7 (.a(Inst[5:0]), .b(6'b000010), .eq(comparator_7_eq));  // open: gt, lt
  Comparator #(.width(6)) comparator_8 (.a(Inst[5:0]), .b(6'b101010), .eq(comparator_8_eq));  // open: gt, lt
  Comparator #(.width(6)) comparator_9 (.a(Inst[5:0]), .b(6'b100100), .eq(comparator_9_eq));  // open: gt, lt
  Comparator #(.width(6)) comparator_10 (.a(Inst[5:0]), .b(6'b100101), .eq(comparator_10_eq));  // open: gt, lt
  Comparator #(.width(6)) comparator_11 (.a(Inst[5:0]), .b(6'b100110), .eq(comparator_11_eq));  // open: gt, lt
  Comparator #(.width(6)) comparator_12 (.a(Inst[5:0]), .b(6'b100111), .eq(comparator_12_eq));  // open: gt, lt
  Multiplexer #(.width(4)) multiplexer_1 (.in0(4'b0000), .in1(4'b0001), .out(multiplexer_1_out), .sel(comparator_1_eq));
  Multiplexer #(.width(4)) multiplexer_2 (.in0(4'b0000), .in1(4'b0010), .out(multiplexer_2_out), .sel(comparator_2_eq));
  Multiplexer #(.width(4)) multiplexer_3 (.in0(4'b0000), .in1(4'b0011), .out(multiplexer_3_out), .sel(comparator_3_eq));
  Multiplexer #(.width(4)) multiplexer_4 (.in0(4'b0000), .in1(4'b0100), .out(multiplexer_4_out), .sel(comparator_4_eq));
  Multiplexer #(.width(4)) multiplexer_5 (.in0(4'b0000), .in1(4'b0101), .out(multiplexer_5_out), .sel(comparator_5_eq));
  Multiplexer #(.width(4)) multiplexer_6 (.in0(4'b0000), .in1(4'b0110), .out(multiplexer_6_out), .sel(comparator_6_eq));
  or or_1 (or_1_out, comparator_6_eq, comparator_7_eq);
  Multiplexer #(.width(4)) multiplexer_7 (.in0(4'b0000), .in1(4'b0111), .out(multiplexer_7_out), .sel(comparator_7_eq));
  Multiplexer #(.width(4)) multiplexer_8 (.in0(4'b0000), .in1(4'b1000), .out(multiplexer_8_out), .sel(comparator_8_eq));
  Multiplexer #(.width(4)) multiplexer_9 (.in0(4'b0000), .in1(4'b1001), .out(multiplexer_9_out), .sel(comparator_9_eq));
  Multiplexer #(.width(4)) multiplexer_10 (
    .in0(4'b0000), .in1(4'b1010), .out(multiplexer_10_out), .sel(comparator_10_eq));
  Multiplexer #(.width(4)) multiplexer_11 (
    .in0(4'b0000), .in1(4'b1011), .out(multiplexer_11_out), .sel(comparator_11_eq));
  Multiplexer #(.width(4)) multiplexer_12 (
    .in0(4'b0000), .in1(4'b1100), .out(multiplexer_12_out), .sel(comparator_12_eq));
  Comparator #(.mode("unsigned"), .width(6)) comparator_13 (
    .a(Inst[31:26]), .b({6{1'b0}}), .gt(comparator_13_gt), .eq(comparator_13_eq), .lt(comparator_13_lt));
  or or_2 (or_2_out, comparator_2_eq, comparator_3_eq);
  not not_1 (not_1_out, or_2_out);
  Comparator #(.width(6)) comparator_14 (.a(Inst[31:26]), .b(6'b001100), .eq(comparator_14_eq));  // open: gt, lt
  Comparator #(.width(6)) comparator_15 (.a(Inst[31:26]), .b(6'b001101), .eq(comparator_15_eq));  // open: gt, lt
  Comparator #(.width(6)) comparator_16 (.a(Inst[31:26]), .b(6'b001110), .eq(comparator_16_eq));  // open: gt, lt
  assign or_3_out = multiplexer_1_out | multiplexer_2_out | multiplexer_3_out | multiplexer_4_out | multiplexer_5_out | multiplexer_6_out | multiplexer_7_out | multiplexer_8_out | multiplexer_9_out | multiplexer_10_out | multiplexer_11_out | multiplexer_12_out;  // OR_Gate or_3, 4 bits wide
  or or_4 (or_4_out, comparator_13_gt, comparator_13_eq);
  or or_5 (or_5_out, comparator_13_gt, comparator_13_eq);
  Multiplexer #(.width(4)) multiplexer_13 (
    .in0(4'b0000), .in1(4'b1001), .out(multiplexer_13_out), .sel(comparator_14_eq));
  Multiplexer #(.width(4)) multiplexer_14 (
    .in0(4'b0000), .in1(4'b1010), .out(multiplexer_14_out), .sel(comparator_15_eq));
  Multiplexer #(.width(4)) multiplexer_15 (
    .in0(4'b0000), .in1(4'b1011), .out(multiplexer_15_out), .sel(comparator_16_eq));
  Multiplexer #(.width(5)) multiplexer_16 (
    .in0({5{1'b0}}), .in1(Inst[25:21]), .out(multiplexer_16_out), .sel(or_4_out));
  Multiplexer #(.width(5)) multiplexer_17 (
    .in0({5{1'b0}}), .in1(Inst[20:16]), .out(multiplexer_17_out), .sel(or_5_out));
  Multiplexer #(.width(5)) multiplexer_18 (
    .in0(Inst[15:11]), .in1(Inst[20:16]), .out(multiplexer_18_out), .sel(comparator_13_gt));
  Comparator #(.width(6)) comparator_17 (.a(Inst[31:26]), .b(6'b001001), .eq(comparator_17_eq));  // open: gt, lt
  assign bit_extender_1_out = {{16{Inst[15]}}, Inst[15:0]};  // Bit_Extender bit_extender_1
  Comparator #(.width(6)) comparator_18 (.a(Inst[31:26]), .b(6'b000011), .eq(comparator_18_eq));  // open: gt, lt
  Comparator #(.width(6)) comparator_19 (.a(Inst[31:26]), .b({6{1'b0}}), .eq(comparator_19_eq));  // open: gt, lt
  Comparator #(.width(6)) comparator_20 (.a(Inst[5:0]), .b(6'b001001), .eq(comparator_20_eq));  // open: gt, lt
  Comparator #(.width(6)) comparator_21 (.a(Inst[31:26]), .b(6'b101011), .eq(mem_we));  // open: gt, lt
  Comparator #(.width(6)) comparator_22 (.a(Inst[31:26]), .b(6'b100011), .eq(comparator_22_eq));  // open: gt, lt
  Comparator #(.width(6)) comparator_23 (.a(Inst[31:26]), .b(6'b000100), .eq(comparator_23_eq));  // open: gt, lt
  Comparator #(.width(6)) comparator_24 (.a(Inst[31:26]), .b(6'b000101), .eq(BNE_sel));  // open: gt, lt
  Comparator #(.width(6)) comparator_25 (.a(Inst[31:26]), .b({6{1'b0}}), .eq(comparator_25_eq));  // open: gt, lt
  Comparator #(.width(6)) comparator_26 (.a(Inst[5:0]), .b(6'b001000), .eq(comparator_26_eq));  // open: gt, lt
  Comparator #(.width(6)) comparator_27 (.a(Inst[31:26]), .b(6'b000010), .eq(comparator_27_eq));  // open: gt, lt
  assign or_6_out = multiplexer_13_out | multiplexer_14_out | multiplexer_15_out;  // OR_Gate or_6, 4 bits wide
  Multiplexer #(.width(5)) multiplexer_19 (
    .in0(multiplexer_16_out), .in1({5{1'b0}}), .out(multiplexer_19_out), .sel(comparator_17_eq));
  Multiplexer #(.width(5)) multiplexer_20 (
    .in0(multiplexer_18_out), .in1(5'b10000), .out(multiplexer_20_out), .sel(comparator_17_eq));
  Multiplexer #(.width(32)) multiplexer_21 (
    .in0({32{1'b0}}), .in1(bit_extender_1_out), .out(multiplexer_21_out), .sel(comparator_13_gt));
  assign bit_extender_2_out = {{27{Inst[10]}}, Inst[10:6]};  // Bit_Extender bit_extender_2
  and and_1 (and_1_out, comparator_19_eq, comparator_20_eq);
  and and_2 (read_ram, comparator_13_gt, comparator_22_eq);
  and and_3 (and_3_out, comparator_25_eq, comparator_26_eq);
  Multiplexer #(.width(4)) multiplexer_22 (
    .in0(4'b0000), .in1(or_3_out), .out(multiplexer_22_out), .sel(comparator_13_eq));
  and and_4 (and_4_out, not_2_out, or_1_out);
  Multiplexer #(.width(5)) multiplexer_23 (.in0(multiplexer_20_out), .in1({5{1'b1}}), .out(rd), .sel(comparator_18_eq));
  Multiplexer #(.width(32)) multiplexer_24 (
    .in0(multiplexer_21_out), .in1(bit_extender_2_out), .out(imm), .sel(and_5_out));
  and and_5 (and_5_out, not_3_out, or_1_out);
  Multiplexer #(.width(4)) multiplexer_25 (
    .in0(multiplexer_22_out), .in1(or_6_out), .out(ALU_code), .sel(comparator_13_gt));
  Multiplexer #(.width(5)) multiplexer_26 (
    .in0(multiplexer_19_out), .in1(multiplexer_17_out), .out(rs), .sel(and_4_out));
  not not_2 (not_2_out, comparator_13_gt);
  Multiplexer #(.width(5)) multiplexer_27 (
    .in0(multiplexer_17_out), .in1(multiplexer_19_out), .out(rt), .sel(and_4_out));
  not not_3 (not_3_out, comparator_13_gt);
  or or_7 (j_reg_select, and_1_out, and_3_out);
  or or_8 (jal_select, and_1_out, comparator_18_eq);
  or or_9 (or_9_out, comparator_18_eq, and_1_out, read_ram);
  or or_10 (Branch, comparator_23_eq, BNE_sel);
  or or_11 (imm_sel, comparator_13_gt, or_1_out);
  or or_12 (or_12_out, or_9_out, not_1_out);
  or or_13 (J_type, comparator_27_eq, j_reg_select, jal_select);
  not not_4 (not_4_out, Branch);
  and and_6 (and_6_out, not_4_out, or_12_out);
  Multiplexer multiplexer_28 (.in0(and_6_out), .in1(1'b0), .out(reg_write_e), .sel(mem_we));

  // Notes on the sheet:
  //   Inst: initial=0x35080002
  //   OP code
  //   rs
  //   shamt
  //   func
  //   sub
  //   mult
  //   div
  //   mflo
  //   mfhi
  //   sll
  //   srl
  //   slt
  //   and
  //   or
  //   xor
  //   nor
  //   rt
  //   rd
  //   I-type
  //   R-type
  //   not mult or div
  //   andi
  //   ori
  //   xori
  //   func
  //   syscall func
  //   op code
  //   jal op
  //   op
  //   jalr op
  //   func
  //   jalr func
  //   func
  //   sw
  //   func
  //   lw
  //   func
  //   beq
  //   func
  //   bne
  //   op
  //   jr op
  //   func
  //   jr func
  //   opcode
  //   j
  //   syscall
  //   if srl/sll, then use SHAMT only
  //   jal
  //   jr
  //   jalr
  //   R-type ALU select
  //   sycall
  //   not mult or div
  //   I-type ALU select
  //   srl/sll AND NOT immediate
  //   lw
  //   jal/jalr/lw
  //   branch
  //   not branch but either jal/jalr/lw or I-type(except mult/div)
endmodule
