// Logisim project ProjectBusLayout.circ as structural Verilog: 10 circuits, main circuit Computer
module Computer (
);

  wire button_1_out, buttoncontroller_1_wetobus, buzzercontroller_1_enablesound, clock_1_out, clock_2_out,
       clock_3_out, clock_4_out, cpu_1_buswriteenable, joystickcontroller_1_wetobus, keyboard_1_avail,
       keyboardcontroller_1_keyboardread, keyboardcontroller_1_writetobus, ledcontroller_1_led_we,
       memorycontroller_1_writeenabletomem, memorycontroller_1_writetobus, rgb_video_1_p2,
       terminalcontroller_1_writetoterminal;
  wire [3:0] undriven, undriven_2;
  wire [6:0] buzzercontroller_1_volume, keyboard_1_data, terminalcontroller_1_datatoterminal;
  wire [7:0] rgb_video_1_p3, rgb_video_1_p4;
  wire [13:0] buzzercontroller_1_frequency;
  wire [23:0] memorycontroller_1_addresstomem, rgb_video_1_p5;
  wire [25:0] cpu_1_addresstobus;
  wire [31:0] buttoncontroller_1_datatobus, controlled_buffer_1_out, cpu_1_datatobus,
       joystickcontroller_1_datatobus, keyboardcontroller_1_datatobus, memorycontroller_1_datatobus,
       memorycontroller_1_datatomem, ram_1_dout;

  RAM #(.addrWidth(24), .dataWidth(32), .enables("line")) ram_1 (
    .addr(memorycontroller_1_addresstomem), .we(memorycontroller_1_writeenabletomem), .clk(clock_1_out),
    .din(memorycontroller_1_datatomem), .dout(ram_1_dout));
  Clock clock_1 (.out(clock_1_out));
  // Probe on memorycontroller_1_addresstomem
  // Probe on ram_1_dout
  // Probe on undriven
  CPU cpu_1 (
    .DataFromBus(controlled_buffer_1_out), .AddressToBus(cpu_1_addresstobus),
    .BusWriteEnable(cpu_1_buswriteenable), .DataToBus(cpu_1_datatobus));
  // Probe on keyboard_1_data
  Clock clock_2 (.out(clock_2_out));
  Keyboard keyboard_1 (
    .clk(clock_2_out), .re(keyboardcontroller_1_keyboardread), .avail(keyboard_1_avail),
    .data(keyboard_1_data));  // open: clr
  Joystick joystick_1 ();  // open: x, y
  Button button_1 (.out(button_1_out));
  MemoryController memorycontroller_1 (
    .WriteEnableFromBus(cpu_1_buswriteenable), .AddressFromBus(cpu_1_addresstobus),
    .DataFromBus(controlled_buffer_1_out), .DataFromMem(ram_1_dout),
    .AddressToMem(memorycontroller_1_addresstomem), .WriteEnableToMem(memorycontroller_1_writeenabletomem),
    .WriteToBus(memorycontroller_1_writetobus), .DataToMem(memorycontroller_1_datatomem),
    .DataToBus(memorycontroller_1_datatobus));
  JoystickController joystickcontroller_1 (
    .WeFromBus(cpu_1_buswriteenable), .AdressFromBus(cpu_1_addresstobus), .X(undriven), .Y(undriven_2),
    .DataFromBus(controlled_buffer_1_out), .DataToBus(joystickcontroller_1_datatobus),
    .WeToBus(joystickcontroller_1_wetobus));
  ButtonController buttoncontroller_1 (
    .DataFromBus(controlled_buffer_1_out), .AddressFromBus(cpu_1_addresstobus),
    .WEFromBus(cpu_1_buswriteenable), .OnPress(button_1_out), .DataToBus(buttoncontroller_1_datatobus),
    .WEToBus(buttoncontroller_1_wetobus));
  assign controlled_buffer_1_out = memorycontroller_1_writetobus ? memorycontroller_1_datatobus : 32'bz;  // Controlled_Buffer controlled_buffer_1
  // Probe on cpu_1_addresstobus
  assign controlled_buffer_1_out = cpu_1_buswriteenable ? cpu_1_datatobus : 32'bz;  // Controlled_Buffer controlled_buffer_2
  KeyboardController keyboardcontroller_1 (
    .DataFromBus(controlled_buffer_1_out), .WriteEnableFromBus(cpu_1_buswriteenable),
    .AddressFromBus(cpu_1_addresstobus), .KeyboardData(keyboard_1_data), .KeyboardStatus(keyboard_1_avail),
    .DataToBus(keyboardcontroller_1_datatobus), .WriteToBus(keyboardcontroller_1_writetobus),
    .KeyboardRead(keyboardcontroller_1_keyboardread));
  assign controlled_buffer_1_out = keyboardcontroller_1_writetobus ? keyboardcontroller_1_datatobus : 32'bz;  // Controlled_Buffer controlled_buffer_3
  assign controlled_buffer_1_out = joystickcontroller_1_wetobus ? joystickcontroller_1_datatobus : 32'bz;  // Controlled_Buffer controlled_buffer_4
  // Probe on controlled_buffer_1_out
  assign controlled_buffer_1_out = buttoncontroller_1_wetobus ? buttoncontroller_1_datatobus : 32'bz;  // Controlled_Buffer controlled_buffer_5
  // Probe on controlled_buffer_1_out
  // Probe on cpu_1_addresstobus
  // Probe on cpu_1_buswriteenable
  Clock clock_3 (.out(clock_3_out));
  // RGB_Video #(.height(256), .width(256)) rgb_video_1: pin names not known; wires that end beside it: clock_3_out, rgb_video_1_p2, rgb_video_1_p3, rgb_video_1_p4, rgb_video_1_p5
  // Probe on terminalcontroller_1_writetoterminal
  Clock clock_4 (.out(clock_4_out));
  TerminalController terminalcontroller_1 (
    .WriteEnableFromBus(cpu_1_buswriteenable), .AddressFromBus(cpu_1_addresstobus),
    .DataFromBus(controlled_buffer_1_out), .WriteToTerminal(terminalcontroller_1_writetoterminal),
    .DataToTerminal(terminalcontroller_1_datatoterminal));
  RGBController rgbcontroller_1 (
    .DataFromBus(controlled_buffer_1_out), .WriteEnable(cpu_1_buswriteenable),
    .AddressFromBus(cpu_1_addresstobus), .RGBX(rgb_video_1_p3), .RGBY(rgb_video_1_p4),
    .RGBColor(rgb_video_1_p5), .RGBWrite(rgb_video_1_p2));
  BuzzerController buzzercontroller_1 (
    .DataFromBus(controlled_buffer_1_out), .WE_FromBus(cpu_1_buswriteenable),
    .AddressFromBus(cpu_1_addresstobus), .Frequency(buzzercontroller_1_frequency),
    .Volume(buzzercontroller_1_volume), .EnableSound(buzzercontroller_1_enablesound));
  // Buzzer buzzer_1: pin names not known; wires that end beside it: buzzercontroller_1_frequency, buzzercontroller_1_enablesound, buzzercontroller_1_volume
  LED led_1 (.in(ledcontroller_1_led_we));
  LEDController ledcontroller_1 (
    .DataFromBus(controlled_buffer_1_out), .WriteEnableFromBus(cpu_1_buswriteenable),
    .AddressFromBus(cpu_1_addresstobus), .LED_we(ledcontroller_1_led_we));
  TTY tty_1 (
    .data(terminalcontroller_1_datatoterminal), .clk(clock_4_out), .we(terminalcontroller_1_writetoterminal));  // open: clr

  // Notes on the sheet:
  //   Write_enable
  //   Address
  //   Data
  //   Data
  //   Address
  //   Write_enable
endmodule

module CPU (
  input  [31:0] DataFromBus,
  output [25:0] AddressToBus,
  output BusWriteEnable,
  output [31:0] DataToBus
);

  wire and_1_out, and_2_out, and_3_out, clock_1_out, clock_2_out, comparator_1_eq, control_1_bne_sel,
       control_1_branch, control_1_imm_sel, control_1_j_reg_select, control_1_j_type, control_1_jal_select,
       control_1_read_ram, control_1_reg_write_e, not_1_out, not_2_out, or_1_out;
  wire [3:0] control_1_alu_code;
  wire [4:0] control_1_rd, control_1_rs, control_1_rt;
  wire [15:0] bit_extender_3_out, rom_1_data, rom_1_data_2;
  wire [25:0] bit_extender_4_out, shifter_2_out;
  wire [31:0] adder_1_out, adder_2_out, alu_1_res, bit_extender_1_out, bit_extender_2_out, control_1_imm,
       multiplexer_1_out, multiplexer_2_out, multiplexer_3_out, multiplexer_4_out, multiplexer_5_out,
       multiplexer_6_out, regfile_1_rs_data, register_1_q, shifter_1_out, shifter_3_out, shifter_4_out;

  Adder #(.width(32)) adder_1 (.a(register_1_q), .b(32'h4), .out(adder_1_out));  // open: cin, cout
  assign bit_extender_1_out = {{16{rom_1_data[15]}}, rom_1_data};  // Bit_Extender bit_extender_1
  // Probe on adder_1_out
  Shifter #(.width(32)) shifter_1 (.in(bit_extender_1_out), .\dist (5'b00010), .out(shifter_1_out));
  // Probe on shifter_1_out
  Shifter #(.width(26)) shifter_2 (.in(bit_extender_4_out), .\dist (5'b00010), .out(shifter_2_out));
  Adder #(.width(32)) adder_2 (.a(adder_1_out), .b(shifter_1_out), .out(adder_2_out));  // open: cin, cout
  assign bit_extender_2_out = {{6{shifter_2_out[25]}}, shifter_2_out};  // Bit_Extender bit_extender_2
  Multiplexer #(.width(32)) multiplexer_1 (
    .in0(adder_1_out), .in1(adder_2_out), .out(multiplexer_1_out), .sel(and_1_out));
  Multiplexer #(.width(32)) multiplexer_2 (
    .in0(bit_extender_2_out), .in1(regfile_1_rs_data), .out(multiplexer_2_out), .sel(control_1_j_reg_select));
  Shifter #(.shift("lr"), .width(32)) shifter_3 (.in(register_1_q), .\dist (5'b00010), .out(shifter_3_out));
  Register #(.width(32)) register_1 (
    .D(multiplexer_3_out), .en(1'b1), .clk(clock_1_out), .Q(register_1_q));  // open: clr
  Multiplexer #(.width(32)) multiplexer_3 (
    .in0(multiplexer_1_out), .in1(multiplexer_2_out), .out(multiplexer_3_out), .sel(control_1_j_type));
  Clock clock_1 (.out(clock_1_out));
  // Probe on regfile_1_rs_data
  Bit_Extender #(.in_width(32)) bit_extender_3 (.in(shifter_3_out), .out(bit_extender_3_out));
  ROM #(.addrWidth(16), .dataWidth(32)) rom_1 (.addr(bit_extender_3_out), .data({rom_1_data_2, rom_1_data}));
  // Probe on {rom_1_data_2, rom_1_data}
  Bit_Extender #(.in_width(32), .out_width(26)) bit_extender_4 (
    .in({rom_1_data_2, rom_1_data}), .out(bit_extender_4_out));
  and and_1 (and_1_out, control_1_branch, or_1_out);
  or or_1 (or_1_out, and_2_out, and_3_out);
  and and_2 (and_2_out, comparator_1_eq, not_1_out);
  and and_3 (and_3_out, not_2_out, control_1_bne_sel);
  not not_1 (not_1_out, control_1_bne_sel);
  not not_2 (not_2_out, comparator_1_eq);
  Multiplexer #(.width(32)) multiplexer_4 (
    .in0(alu_1_res), .in1(DataFromBus), .out(multiplexer_4_out), .sel(control_1_read_ram));
  // Probe on {rom_1_data_2, rom_1_data}
  Multiplexer #(.width(32)) multiplexer_5 (
    .in0(multiplexer_4_out), .in1(adder_1_out), .out(multiplexer_5_out), .sel(control_1_jal_select));
  Control control_1 (
    .Inst({rom_1_data_2, rom_1_data}), .rs(control_1_rs), .rt(control_1_rt), .rd(control_1_rd),
    .imm(control_1_imm), .reg_write_e(control_1_reg_write_e), .imm_sel(control_1_imm_sel),
    .mem_we(BusWriteEnable), .read_ram(control_1_read_ram), .Branch(control_1_branch),
    .BNE_sel(control_1_bne_sel), .j_reg_select(control_1_j_reg_select), .jal_select(control_1_jal_select),
    .J_type(control_1_j_type), .ALU_code(control_1_alu_code));
  regfile regfile_1 (
    .write_e(control_1_reg_write_e), .rd(control_1_rd), .rs(control_1_rs), .rt(control_1_rt),
    .rd_data(multiplexer_5_out), .rs_data(regfile_1_rs_data), .rt_data(DataToBus));
  Comparator #(.width(32)) comparator_1 (.a(regfile_1_rs_data), .b(DataToBus), .eq(comparator_1_eq));  // open: gt, lt
  Multiplexer #(.width(32)) multiplexer_6 (
    .in0(DataToBus), .in1(control_1_imm), .out(multiplexer_6_out), .sel(control_1_imm_sel));
  // Probe on alu_1_res
  ALU alu_1 (.OP1(regfile_1_rs_data), .OP2(multiplexer_6_out), .ALU_CODE(control_1_alu_code), .Res(alu_1_res));
  Bit_Extender #(.in_width(32), .out_width(26)) bit_extender_5 (.in(shifter_4_out), .out(AddressToBus));
  Shifter #(.shift("lr"), .width(32)) shifter_4 (.in(alu_1_res), .\dist (5'b00010), .out(shifter_4_out));
  Clock clock_2 (.out(clock_2_out));

  // Notes on the sheet:
  //   PC adder + 4
  //   label or j/jal (word addressed)
  //   Branch
  //   offset
  //   rs for jr/jalr (byte addressed)
  //   jr/jalr
  //   any j
  //   j
  //   contents of rom_1 (hex, n*v repeats v):
  //   1040000f 201b0001 105b0011 201b0005 105b0048 201b0009 105b0066 201b000a 105b0068 201b000b 105b0067
  //   201b000c 105b0067 201b000d 105b006c 8000071 201df000 201b008c ac1bf000 800007f 23bdfffc afbf0000
  //   80082a 10010005 201b002d ac1bff00 3884ffff 20840001 8000020 14800002 ac04ff00 8000048 201b2710
  //   9b082a 1001000b 201b03e8 9b082a 1001000e 201b0064 9b082a 10010011 201b000a 9b082a 10010014 201b0001
  //   8000046 201b2710 9b001a d812 237b0030 ac1bff00 2010 201b03e8 9b001a d812 237b0030 ac1bff00 2010
  //   201b0064 9b001a d812 237b0030 ac1bff00 2010 201b000a 9b001a d812 237b0030 ac1bff00 2010 20840030
  //   ac04ff00 201b000a ac04ff00 8fbf0000 23bd0004 3400008 23bdfffc afbf0000 8c1bff10 13600019 8c1bff14
  //   2001002d 3b082a 361082a 210825 38210001 20020000 2008000a 237bffd0 360082a 14010001 23620000
  //   ac00ff10 8c1bff14 13680005 237bffd0 480018 1012 5b1020 800005d ac00ff10 10200003 2001ffff 410018
  //   1012 8fbf0000 23bd0004 3400008 8c02f000 44d820 ac1bf000 3400008 8000071 ac04ff00 3400008 20020000
  //   14020002 8c02ff14 8000075 8c02ff14 ac00ff10 3400008 20020000 8c02ff40 ac02ff30 3400008 201df000
  //   20080009 20090027 200a0078 ac0aff24 21080001 ac08ff20 ac00ff2c 128682a 11a0fffb 20080009 20090027
  //   200a0088 ac0aff24 21080001 ac08ff20 ac00ff2c 128682a 11a0fffb 20080077 20090087 200a000a ac0aff20
  //   21080001 ac08ff24 ac00ff2c 128682a 11a0fffb 20080077 20090087 200a0028 ac0aff20 21080001 ac08ff24
  //   ac00ff2c 128682a 11a0fffb 200800ff 84a00 85400 149f020 20197fc8 2010007e 2011000c 2012007e 20130026
  //   22240000 22050000 c000102 22640000 22450000 c000102 c000192 20140080 20150019 20160000 20170002
  //   ac15ff20 ac14ff24 ac00ff2c 2009000c 200a0026 2a9402a 150000a7 155402a 1500009f 2002000d d009
  //   10400007 20080068 8d090000 21290001 200a0009 152a0001 2129fff7 ad090000 22640000 22450000 22a60000
  //   22870000 c000146 10400000 22240000 22050000 22a60000 22870000 c000146 10400000 8c08ff10 11000027
  //   8c08ff14 20090077 15090007 2008007a 12080004 22240000 22050000 c000116 2210ffff 80000ff 20090073
  //   15090008 20080087 22090005 11280004 22240000 22050000 c000120 22100001 80000ff 20090069 15090007
  //   2008007a 12480004 22640000 22450000 c000116 2252ffff 80000ff 2009006b 15090007 20080087 22490005
  //   11280004 22640000 22450000 c000120 22520001 ac00ff10 c000129 80000bb ac00ff28 20a80000 20a90005
  //   ac04ff20 ac08ff24 ac00ff2c 21080001 109502a 15400005 3e00008 ac1eff28 20a80000 20a90005 ac04ff20
  //   ac08ff24 ac00ff2c 21080001 109502a 1540fffb 3e00008 ac04ff20 20a80004 ac08ff24 ac1eff28 ac00ff2c
  //   20a8ffff ac08ff24 ac00ff28 ac00ff2c 3e00008 ac04ff20 ac05ff24 ac1eff28 ac00ff2c 20a80005 ac08ff24
  //   ac00ff28 ac00ff2c 3e00008 ac15ff20 ac14ff24 ac1eff28 ac00ff2c 296a020 2b7a820 20080079 288482a
  //   11200002 16b022 21140001 20080087 114482a 11200002 16b022 2114ffff 20080068 8d080000 20090004
  //   1090018 4012 2009006c 1284820 8d280000 ac15ff20 ac14ff24 ac08ff28 ac00ff2c 3e00008 20880001 106482a
  //   15200015 2088ffff c8482a 15200012 e5402a 15000010 20aa0004 147402a 1500000d 80001cd 20084e6d
  //   20093039 200a0005 3280018 c812 329c820 32a001a 6010 2196fffe 17b822 20020001 3e00008 20020000
  //   3e00008 20090000 8d2a0000 214a0001 ad2a0000 20080001 800016c 20090000 8d2a0004 214a0001 ad2a0004
  //   20080002 800016c 2002000b 20090008 8d2a001c 210a0030 ad2a001c c0001dc 200b000a 8d240000 d009
  //   108b0002 21290004 8000173 20090040 200a0000 8d4c0000 218c0030 ad2c0008 8d4c0004 218c0030 ad2c0018
  //   8d240000 d009 108b0002 21290004 8000180 d009 8000187 22240000 22050000 c00010c 22640000 22450000
  //   c00010c ac15ff20 ac14ff24 ac1eff28 ac00ff2c 80000a9 200e0032 ac0eff84 ac00ff88 200e020b 200f000f
  //   ac0eff80 100f0002 21efffff 8000198 200e0293 200f000f ac0eff80 100f0002 21efffff 800019e 200e0310
  //   200f000f ac0eff80 100f0002 21efffff 80001a4 200e0417 200f001e ac0eff80 100f0002 21efffff 80001aa
  //   200f000f ac00ff88 100f0002 21efffff 80001af 200e0310 ac0eff80 ac00ff88 200f000f 100f0002 21efffff
  //   80001b6 200f000f 200e0370 ac0eff80 100f0002 21efffff 80001bc 200f000f 200e0310 ac0eff80 100f0002
  //   21efffff 80001c2 200e0417 200f0028 ac0eff80 100f0002 21efffff 80001c8 ac00ff88 3e00008 ac00ff88
  //   200e02bc ac0eff80 200f0002 100f00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
  //   0028 a
  //   002d s
  //   0033 d
  //   0020 is where loop begins
  //   0039 is where colorchange begins
  //   j_reg
  //   ? is this right
  //   beq
  //   bne
  //   jal/jalr
  //   beq/bne
endmodule

module MemoryController (
  input  WriteEnableFromBus,
  input  [25:0] AddressFromBus,
  input  [31:0] DataFromBus,
  input  [31:0] DataFromMem,
  output [23:0] AddressToMem,
  output WriteEnableToMem,
  output WriteToBus,
  output [31:0] DataToMem,
  output [31:0] DataToBus
);

  wire comparator_1_lt, not_1_out;

  Comparator #(.mode("unsigned"), .width(26)) comparator_1 (
    .a(AddressFromBus), .b(26'h3ffff00), .lt(comparator_1_lt));  // open: gt, eq
  not not_1 (not_1_out, WriteEnableFromBus);
  Bit_Extender #(.in_width(26), .out_width(24)) bit_extender_1 (.in(AddressFromBus), .out(AddressToMem));
  and and_1 (WriteEnableToMem, WriteEnableFromBus, comparator_1_lt);
  and and_2 (WriteToBus, not_1_out, comparator_1_lt);

  assign DataToBus = DataFromMem;
  assign DataToMem = DataFromBus;

  // Notes on the sheet:
  //   WE from bus <- 1 for sw or 0 for lw
endmodule

module KeyboardController (
  input  WriteEnableFromBus,
  input  [25:0] AddressFromBus,
  input  [6:0] KeyboardData,
  input  KeyboardStatus,
  input  [31:0] DataFromBus,
  output KeyboardRead,
  output [31:0] DataToBus,
  output WriteToBus
);

  wire and_2_out, and_3_out, comparator_1_eq, comparator_2_eq, not_1_out, not_2_out;
  wire [25:0] shifter_1_out;
  wire [31:0] bit_extender_1_out, bit_extender_2_out, multiplexer_1_out;

  // Probe on shifter_1_out
  assign bit_extender_1_out = {{25{1'b0}}, KeyboardData};  // Bit_Extender bit_extender_1
  assign bit_extender_2_out = {{31{1'b0}}, KeyboardStatus};  // Bit_Extender bit_extender_2
  Shifter #(.width(26)) shifter_1 (.in(AddressFromBus), .\dist (5'b00010), .out(shifter_1_out));
  Comparator #(.width(26)) comparator_1 (.a(shifter_1_out), .b(26'h3ffff10), .eq(comparator_1_eq));  // open: gt, lt
  Comparator #(.width(26)) comparator_2 (.a(shifter_1_out), .b(26'h3ffff14), .eq(comparator_2_eq));  // open: gt, lt
  and and_1 (KeyboardRead, WriteEnableFromBus, comparator_1_eq);
  not not_1 (not_1_out, WriteEnableFromBus);
  and and_2 (and_2_out, not_1_out, comparator_1_eq);
  and and_3 (and_3_out, comparator_2_eq, not_2_out);
  not not_2 (not_2_out, WriteEnableFromBus);
  Multiplexer #(.width(32)) multiplexer_1 (
    .in0(bit_extender_1_out), .in1(bit_extender_2_out), .out(multiplexer_1_out), .sel(and_2_out));
  Multiplexer #(.width(32)) multiplexer_2 (
    .in0(multiplexer_1_out), .in1(bit_extender_1_out), .out(DataToBus), .sel(and_3_out));
  or or_1 (WriteToBus, and_2_out, and_3_out);

  // Notes on the sheet:
  //   1 -> sw
  //   1 -> lw / 0 -> sw
  //    1 -> lw
  //   1 for any lw
endmodule

module RGBController (
  input  [31:0] DataFromBus,
  input  WriteEnable,
  input  [25:0] AddressFromBus,
  output [7:0] RGBX,
  output [7:0] RGBY,
  output [23:0] RGBColor,
  output RGBWrite
);

  wire and_1_out, and_2_out, and_3_out, clock_1_out, comparator_1_eq, comparator_2_eq, comparator_3_eq,
       comparator_4_eq;
  wire [7:0] bit_extender_1_out, bit_extender_2_out;
  wire [23:0] bit_extender_3_out;
  wire [25:0] shifter_1_out;

  Shifter #(.width(26)) shifter_1 (.in(AddressFromBus), .\dist (5'b00010), .out(shifter_1_out));
  // Probe on shifter_1_out
  Comparator #(.width(26)) comparator_1 (.a(26'h3ffff20), .b(shifter_1_out), .eq(comparator_1_eq));  // open: gt, lt
  Comparator #(.width(26)) comparator_2 (.a(26'h3ffff24), .b(shifter_1_out), .eq(comparator_2_eq));  // open: gt, lt
  Comparator #(.width(26)) comparator_3 (.a(26'h3ffff28), .b(shifter_1_out), .eq(comparator_3_eq));  // open: gt, lt
  Comparator #(.width(26)) comparator_4 (.a(26'h3ffff2c), .b(shifter_1_out), .eq(comparator_4_eq));  // open: gt, lt
  and and_1 (and_1_out, WriteEnable, comparator_1_eq);
  and and_2 (and_2_out, WriteEnable, comparator_2_eq);
  and and_3 (and_3_out, WriteEnable, comparator_3_eq);
  and and_4 (RGBWrite, WriteEnable, comparator_4_eq);
  Bit_Extender #(.in_width(32), .out_width(8)) bit_extender_1 (.in(DataFromBus), .out(bit_extender_1_out));
  Bit_Extender #(.in_width(32), .out_width(8)) bit_extender_2 (.in(DataFromBus), .out(bit_extender_2_out));
  Bit_Extender #(.in_width(32), .out_width(24)) bit_extender_3 (.in(DataFromBus), .out(bit_extender_3_out));
  Register x_coord (.D(bit_extender_1_out), .en(and_1_out), .clk(clock_1_out), .Q(RGBX));  // open: clr
  Register y_coord (.D(bit_extender_2_out), .en(and_2_out), .clk(clock_1_out), .Q(RGBY));  // open: clr
  Register #(.width(24)) RGB (.D(bit_extender_3_out), .en(and_3_out), .clk(clock_1_out), .Q(RGBColor));  // open: clr
  Clock clock_1 (.out(clock_1_out));
endmodule

module TerminalController (
  input  WriteEnableFromBus,
  input  [25:0] AddressFromBus,
  input  [31:0] DataFromBus,
  output WriteToTerminal,
  output [6:0] DataToTerminal
);

  wire comparator_1_eq;
  wire [6:0] bit_extender_1_out;
  wire [25:0] shifter_1_out;

  // Probe on 26'h3ffff00
  Shifter #(.width(26)) shifter_1 (.in(AddressFromBus), .\dist (5'b00010), .out(shifter_1_out));
  // Probe on shifter_1_out
  Comparator #(.width(26)) comparator_1 (.a(shifter_1_out), .b(26'h3ffff00), .eq(comparator_1_eq));  // open: gt, lt
  Bit_Extender #(.in_width(32), .out_width(7)) bit_extender_1 (.in(DataFromBus), .out(bit_extender_1_out));
  and and_1 (WriteToTerminal, WriteEnableFromBus, comparator_1_eq);
  Multiplexer #(.width(7)) multiplexer_1 (
    .in0({7{1'b0}}), .in1(bit_extender_1_out), .out(DataToTerminal), .sel(WriteToTerminal));

  // Notes on the sheet:
  //   2 bit shifter is to translate 24-bit MIPS address to 26-bit "project address"
endmodule

module BuzzerController (
  input  [31:0] DataFromBus,
  input  WE_FromBus,
  input  [25:0] AddressFromBus,
  output [13:0] Frequency,
  output [6:0] Volume,
  output EnableSound
);

  wire and_1_out, and_2_out, and_3_out, clock_1_out, comparator_1_eq, comparator_2_eq, comparator_3_eq,
       not_1_out;
  wire [6:0] bit_extender_2_out;
  wire [13:0] bit_extender_1_out;
  wire [25:0] shifter_1_out;

  // Probe on 26'h3ffff80
  Shifter #(.width(26)) shifter_1 (.in(AddressFromBus), .\dist (5'b00010), .out(shifter_1_out));
  // Probe on shifter_1_out
  Comparator #(.width(26)) comparator_1 (.a(26'h3ffff80), .b(shifter_1_out), .eq(comparator_1_eq));  // open: gt, lt
  Comparator #(.width(26)) comparator_2 (.a(26'h3ffff84), .b(shifter_1_out), .eq(comparator_2_eq));  // open: gt, lt
  Comparator #(.width(26)) comparator_3 (.a(26'h3ffff88), .b(shifter_1_out), .eq(comparator_3_eq));  // open: gt, lt
  and and_1 (and_1_out, WE_FromBus, comparator_1_eq);
  and and_2 (and_2_out, WE_FromBus, comparator_2_eq);
  and and_3 (and_3_out, WE_FromBus, comparator_3_eq);
  Register #(.width(14)) register_1 (
    .D(bit_extender_1_out), .en(and_1_out), .clk(clock_1_out), .Q(Frequency));  // open: clr
  Register #(.width(7)) register_2 (
    .D(bit_extender_2_out), .en(and_2_out), .clk(clock_1_out), .Q(Volume));  // open: clr
  Register #(.width(1)) register_3 (.D(not_1_out), .en(and_3_out), .clk(clock_1_out), .Q(EnableSound));  // open: clr
  not not_1 (not_1_out, EnableSound);
  Clock clock_1 (.out(clock_1_out));
  Bit_Extender #(.in_width(32), .out_width(14)) bit_extender_1 (.in(DataFromBus), .out(bit_extender_1_out));
  Bit_Extender #(.in_width(32), .out_width(7)) bit_extender_2 (.in(DataFromBus), .out(bit_extender_2_out));
endmodule

module LEDController (
  input  [31:0] DataFromBus,
  input  WriteEnableFromBus,
  input  [25:0] AddressFromBus,
  output LED_we
);

  wire and_1_out, bit_extender_1_out, comparator_1_eq;
  wire [25:0] shifter_1_out;

  // Probe on shifter_1_out
  Bit_Extender #(.in_width(32), .out_width(1), .\type ("zero")) bit_extender_1 (
    .in(DataFromBus), .out(bit_extender_1_out));
  Shifter #(.width(26)) shifter_1 (.in(AddressFromBus), .\dist (5'b00010), .out(shifter_1_out));
  and and_1 (and_1_out, bit_extender_1_out, 1'b1);
  Comparator #(.width(26)) comparator_1 (.a(shifter_1_out), .b(26'h3ffff30), .eq(comparator_1_eq));  // open: gt, lt
  and and_2 (LED_we, and_1_out, WriteEnableFromBus, comparator_1_eq);
endmodule

module JoystickController (
  input  WeFromBus,
  input  [25:0] AdressFromBus,
  input  [3:0] X,
  input  [3:0] Y,
  input  [31:0] DataFromBus,
  output [31:0] DataToBus,
  output WeToBus
);

  wire and_1_out, and_2_out, comparator_1_eq, comparator_2_eq, not_1_out, undriven;
  wire [3:0] multiplexer_1_out;
  wire [25:0] shifter_1_out;

  // Probe on undriven
  not not_1 (not_1_out, WeFromBus);
  Shifter #(.width(26)) shifter_1 (.in(AdressFromBus), .\dist (5'b00010), .out(shifter_1_out));
  Comparator #(.width(26)) comparator_1 (.a(shifter_1_out), .b(26'h3ffff50), .eq(comparator_1_eq));  // open: gt, lt
  Comparator #(.width(26)) comparator_2 (.a(shifter_1_out), .b(26'h3ffff54), .eq(comparator_2_eq));  // open: gt, lt
  and and_1 (and_1_out, not_1_out, comparator_1_eq);
  and and_2 (and_2_out, not_1_out, comparator_2_eq);
  or or_1 (WeToBus, and_2_out, and_1_out);
  Multiplexer #(.width(4)) multiplexer_1 (.in0(4'b0000), .in1(X), .out(multiplexer_1_out), .sel(and_1_out));
  Multiplexer #(.width(4)) multiplexer_2 (.in0(multiplexer_1_out), .in1(Y), .out(DataToBus[3:0]), .sel(and_2_out));
  // Probe on {{28{1'b0}}, DataToBus[3:0]}

  assign DataToBus[31:4] = {28{1'b0}};
endmodule

module ButtonController (
  input  [31:0] DataFromBus,
  input  [25:0] AddressFromBus,
  input  WEFromBus,
  input  OnPress,
  output [31:0] DataToBus,
  output WEToBus
);

  wire comparator_1_eq, not_1_out;
  wire [25:0] shifter_1_out;
  wire [31:0] multiplexer_1_out;

  // Probe on shifter_1_out
  Shifter #(.width(26)) shifter_1 (.in(AddressFromBus), .\dist (5'b00010), .out(shifter_1_out));
  Comparator #(.width(26)) comparator_1 (.a(shifter_1_out), .b(26'h3ffff40), .eq(comparator_1_eq));  // open: gt, lt
  not not_1 (not_1_out, WEFromBus);
  and and_1 (WEToBus, comparator_1_eq, not_1_out, OnPress);
  assign DataToBus = WEToBus ? multiplexer_1_out : 32'bz;  // Controlled_Buffer controlled_buffer_1
  Multiplexer #(.width(32)) multiplexer_1 (.in0(DataFromBus), .in1(32'h1), .out(multiplexer_1_out), .sel(WEToBus));
endmodule
